# Fritzing sketch ClockPCB (saved by Fritzing 0.9.10b)
breadboards: 1

parts:
  DRV_1 = DRV 8825 Stepper Motor Carrier, High Current [part_number="DRV 8825"]
  M1 = Stepper Motor - Bipolar
  LED2 = LED - 3mm [color="Infrared (940nm)" current=0.030 package="3 mm [THT]"]
  J1 = female pin header, 3 pins [form="♀ (female)"]
  U1 = Voltage Regulator - 5V [package="TO220 [THT]"]
  R1 = Resistor [tolerance=±5% resistance=220 package="1206 [SMD]"]
  R2 = Resistor [tolerance=±5% resistance=10k package="1206 [SMD]"]
  Part1 = Adafruit DS3231 [part_number="Adafruit #3013"]
  LED1 = LED - 3mm [color="Infrared (940nm)" current=0.030 package="3 mm [THT]"]
  Mod1 = Amica NodeMCU DEVKIT 1.0

nets:
  N1: DRV_1.ENABLE, Mod1.pin_11
  N2: DRV_1.MS1, Mod1.pin8
  N3: DRV_1.MS2, Mod1.pin7
  N4: DRV_1.MS3, Mod1.pin5
  N5: DRV_1.RESET, DRV_1.SLEEP, J1.pin3, Part1.Vin, LED1.anode, Mod1.pin1, Mod1.pin_10, Mod1.pin_26
  N6: DRV_1.STEP, Mod1.pin_15
  N7: DRV_1.DIRECTION, Mod1.pin_12
  N8: DRV_1.VOLTAGE_ST/_MT, U1.input_voltage
  GND: DRV_1.GROUND_ST/_MT, DRV_1.GROUND_LOG, J1.pin2, U1.GND, R1.Pin_1, R2.Pin_1, Part1.GND, Mod1.pin2, Mod1.pin_9, Mod1.pin_25, Mod1.pin_29
  N9: DRV_1.OUT_2B, M1.A
  N10: DRV_1.OUT_2A, M1.C
  N11: DRV_1.OUT_1A, M1.B
  N12: DRV_1.OUT_1B, M1.D
  N13: LED2.cathode, R2.Pin_0
  N14: LED2.anode, J1.pin1, Mod1.pin6
  N15: U1.output_voltage, Mod1.pin_30
  N16: R1.Pin_0, LED1.cathode
  N17: Part1.SCL, Mod1.pin_14
  N18: Part1.SDA, Mod1.pin_13

custom parts:
  Adafruit DS3231: The datasheet for the DS3231 explains that this part is an "Extremely Accurate I²C-Integrated RTC/TCXO/Crystal". And, hey, it does exactly what it says on the tin! This Real Time Clock (RTC) is the most precise you can get in a small, low power package. Most RTCs use an external 32kHz timing crystal that is used to keep time with low current draw. And that's all well and good, but those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
